// Logisim project AndrewCPU.circ as structural Verilog: 4 circuits, main circuit ALU
module ALU (
  input  [7:0] A,
  input  [7:0] B,
  input  [2:0] in_3,
  output [7:0] Result
);

  wire [7:0] adder_1_out, adder_2_out, adder_3_out, and_1_out, or_1_out, subtractor_1_out;

  assign and_1_out = A & B;  // AND_Gate and_1, 8 bits wide
  assign or_1_out = A | B;  // OR_Gate or_1, 8 bits wide
  Adder adder_1 (.a(A), .b(8'h1), .out(adder_1_out));  // open: cin, cout
  Adder adder_2 (.a(B), .b(8'h1), .out(adder_2_out));  // open: cin, cout
  Adder adder_3 (.a(A), .b(B), .out(adder_3_out));  // open: cin, cout
  Subtractor subtractor_1 (.a(A), .b(B), .out(subtractor_1_out));  // open: bin, bout
  Multiplexer #(.select(3), .width(8), .enable("false")) multiplexer_1 (
    .in0(A), .in1(B), .in2(adder_1_out), .in3(adder_2_out), .in4(adder_3_out), .in5(subtractor_1_out),
    .in6(and_1_out), .in7(or_1_out), .out(Result), .sel(in_3));
endmodule

module main (
);

  wire [7:0] ALU_p3, multiplexer_1_out, registers_a, registers_b, registers_mbr, registers_out;

  Data_Path registers (
    .data(ALU_p3), .a(registers_a), .b(registers_b), .out(registers_out), .mbr(registers_mbr));  // open: write, reg, clear
  Multiplexer #(.select(2), .width(8), .enable("false")) multiplexer_1 (
    .in0(registers_b), .in1(registers_mbr), .out(multiplexer_1_out));  // open: in2, in3, sel
  // ALU ALU: pin names not known; wires that end beside it: registers_a, multiplexer_1_out, ALU_p3
endmodule

module Data_Path (
  input  [7:0] data,
  input  write,
  input  [1:0] \reg ,
  input  clear,
  output [7:0] a,
  output [7:0] b,
  output [7:0] out,
  output [7:0] mbr
);

  wire demultiplexer_1_out0, demultiplexer_1_out1, demultiplexer_1_out2, demultiplexer_1_out3;

  Demultiplexer #(.select(2), .enable("false")) demultiplexer_1 (
    .out0(demultiplexer_1_out0), .out1(demultiplexer_1_out1), .out2(demultiplexer_1_out2),
    .out3(demultiplexer_1_out3), .in(write), .sel(\reg ));
  Register u_A (.D(data), .Q(a), .clk(demultiplexer_1_out0), .clr(clear));  // open: en
  Register u_B (.D(data), .Q(b), .clk(demultiplexer_1_out1), .clr(clear));  // open: en
  Register u_OUT (.D(data), .Q(out), .clk(demultiplexer_1_out2), .clr(clear));  // open: en
  Register u_MBR (.D(data), .Q(mbr), .clk(demultiplexer_1_out3), .clr(clear));  // open: en
endmodule

module Control_Unit (
);

  wire clock_1_out, undriven;
  wire [4:0] MPC_q;
  wire [15:0] MIR_q, ram_1_data;

  Register #(.width(5)) MPC (.D(MIR_q[15:11]), .en(undriven), .Q(MPC_q), .clk(clock_1_out));  // open: clr
  Clock clock_1 (.out(clock_1_out));
  RAM #(.addrWidth(5), .dataWidth(16), .bus("asynch")) ram_1 (.addr(MPC_q), .data(ram_1_data));  // open: sel, ld, clr
  Register #(.width(16)) MIR (.D(ram_1_data), .Q(MIR_q), .clk(clock_1_out));  // open: en, clr
endmodule
